# Fritzing sketch doorOpenerBreadboard (saved by Fritzing 0.9.2b)
breadboards: 1

parts:
  Part1 = iotsa esp-12 experiment board
  Q2 = 2N7000 FET N-Channel [part_number=2N7000 package=TO92]
  R1 = Resistor [tolerance=±5% resistance=10k package=THT]
  R2 = Resistor [tolerance=±1% resistance=100k package=THT]
  D1 = Rectifier Diode [part_number=1N4001 package="300 mil [THT]"]
  L1 = Solenoid
  Part2 = RFID-RC522-v2
  LED1 = prefix0000

nets:
  N1: Part1.pin_10, R1.Pin_0
  N2: Part1.pin_11, Part2.SDA
  N3: Part1.pin_13, Part2.RST
  N4: Part1.pin_14, Part2.SCK
  N5: Part1.pin_15, Part2.MISO
  N6: Part1.pin_16, Part2.MOSI
  N7: Part1.pin_26, Part2.3.3V, LED1.connector1
  N8: Part1.pin_36, D1.cathode, L1.pin2
  N9: Part1.pin_46, Q2.source, R2.Pin_1, Part2.GND, LED1.connector3
  N10: Part1.pin_137, LED1.connector2
  N11: Q2.gate, R1.Pin_1, R2.Pin_0
  N12: Q2.drain, D1.anode, L1.pin1

custom parts:
  iotsa esp-12 experiment board: Board with an ESP-12, a power supply, reset button, FTDI plug and experiment area.
  2N7000 FET N-Channel: A 2N7000 MOSFET N-Channel Transistor
  RFID-RC522-v2: A simple China made RFID-RC522 Reader; do check the pin labels, as this is a MFRC522 based clone.
