# Fritzing sketch doorOpenerIotsaRelay (saved by Fritzing 0.9.2b)

parts:
  Part1 = iotsa esp-12 experiment board
  Q2 = 2N7000 FET N-Channel [part_number=2N7000 package=TO92]  # not connected
  R1 = Resistor [tolerance=±5% resistance=10k package=THT]  # not connected
  R2 = Resistor [tolerance=±1% resistance=100k package=THT]  # not connected
  D1 = Rectifier Diode [part_number=1N4001 package="300 mil [THT]"]  # not connected
  L1 = Solenoid
  Part2 = RFID-RC522-v2
  LED1 = prefix0000
  U1 = IC, SIP package, 7 pins [chip_label=SIP-1A05]

nets:
  N1: Part1.pin_10, Part1.pin_107, Part1.pin_108
  N2: Part1.pin_11, Part1.pin_50, Part1.pin_51, Part2.SDA
  N3: Part1.pin_13, Part1.pin_68, Part1.pin_69, Part2.RST
  N4: Part1.pin_14, Part1.pin_53, Part1.pin_54, Part2.SCK
  N5: Part1.pin_15, Part1.pin_59, Part1.pin_60, Part2.MISO
  N6: Part1.pin_16, Part1.pin_56, Part1.pin_57, Part2.MOSI
  N7: Part1.pin_17, Part1.pin_25, Part1.pin_71, Part1.pin_72, Part2.3.3V, LED1.connector1
  N8: Part1.pin_32, Part1.pin_36, Part1.pin_92, Part1.pin_93, Part1.pin_131, Part1.pin_132, Part1.pin_133, L1.pin2, U1.pin5
  N9: Part1.pin_37, Part1.pin_39, Part1.pin_40, Part1.pin_41, Part1.pin_45, Part1.pin_46, Part1.pin_65, Part1.pin_66, Part1.pin_81, Part1.pin_82, Part1.pin_116, Part1.pin_118, Part2.GND, LED1.connector3, U1.pin1
  N10: Part1.pin_87, Part1.pin_88, Part1.pin_122, Part1.pin_123, Part1.pin_124, U1.pin3
  N11: Part1.pin_99, Part1.pin_100, L1.pin1, U1.pin7
  N12: Part1.pin_110, Part1.pin_112, Part1.pin_137, LED1.connector2
  N13: Part1.pin_119, Part1.pin_120, Part1.pin_121

custom parts:
  iotsa esp-12 experiment board: Board with an ESP-12, a power supply, reset button, FTDI plug and experiment area.
  2N7000 FET N-Channel: A 2N7000 MOSFET N-Channel Transistor
  RFID-RC522-v2: A simple China made RFID-RC522 Reader; do check the pin labels, as this is a MFRC522 based clone.
